# Fritzing sketch LFR_v1 (saved by Fritzing 0.9.3b)
breadboards: 1

parts:
  Part1 = Arduino Nano (Rev3.0)
  IC1 = Voltage Regulator [package=to-220-alt]
  LED1 = LED - 5mm [color="Red (633nm)" package="5 mm [THT]"]
  R1 = Resistor [tolerance=±5% resistance=220 package="2010 [SMD]"]
  Part2 = Motor Driver 1A Dual TB6612FNG
  M1 = DC Motor
  M2 = DC Motor
  U1 = LIPO-110mAh [package=lipo-110]
  J1 = Infrared Proximity Sensor
  J2 = Infrared Proximity Sensor
  J3 = Infrared Proximity Sensor
  J4 = Infrared Proximity Sensor
  J5 = Infrared Proximity Sensor
  J6 = Infrared Proximity Sensor
  J7 = Infrared Proximity Sensor
  S1 = Pushbutton [package=THT]
  S2 = Pushbutton [package=THT]

nets:
  GND: Part1.GND, IC1.GND, LED1.cathode, Part2.GND, U1.-, J1.GND, J2.GND, J3.GND, J4.GND, J5.GND, J6.GND, J7.GND
  N1: Part1.D3, Part2.AIN2
  N2: Part1.D4, Part2.AIN1
  N3: Part1.D6, Part2.BIN1
  N4: Part1.D7, Part2.BIN2
  N5: Part1.D9, Part2.PWMA
  N6: Part1.D10, Part2.PWMB
  N7: Part1.D11/MOSI, S2.leg1
  N8: Part1.D12/MISO, S1.leg1
  VIN: Part1.VIN, IC1.OUT, Part2.VCC
  VCC: Part1.5V, Part2.STBY, J1.Vcc, J2.Vcc, J3.Vcc, J4.Vcc, J5.Vcc, J6.Vcc, J7.Vcc, S1.leg0, S2.leg0
  N9: Part1.A6, J5.Vout
  N10: Part1.A5, J1.Vout
  N11: Part1.A4, J2.Vout
  N12: Part1.A3, J3.Vout
  N13: Part1.A2, J4.Vout
  N14: Part1.A1, J6.Vout
  N15: Part1.A0, J7.Vout
  N16: Part1.D13/SCK, R1.Pin_0
  N17: IC1.IN, Part2.VM, U1.+
  N18: LED1.anode, R1.Pin_1
  N19: Part2.B01, M1.pin_1
  N20: Part2.B02, M1.pin_2
  N21: Part2.A02, M2.pin_2
  N22: Part2.A01, M2.pin_1
